# Fritzing sketch vent (saved by Fritzing 0.9.3b)

parts:
  M1 = BME280
  Part1 = Arduino Uno (Rev3)

nets:
  VIN: M1.VIN, Part1.5V
  GND: M1.GND, Part1.GND
  N1: M1.SCL, Part1.A5/SCL
  N2: M1.SDA, Part1.A4/SDA

custom parts:
  BME280: Temperature Humidity Barometric presure Sensor
