# Fritzing sketch all (saved by Fritzing 0.9.3b)
breadboards: 1

parts:
  M1 = BME280
  Part1 = Arduino Uno (Rev3)
  S1 = Square Pushbutton
  M2 = MAX30102
  A1 = DHT22 module
  M3 = Stepper Motor - Unipolar
  DRV_2 = DRV 8825 Stepper Motor Carrier, High Current [part_number="DRV 8825"]
  VCC2 = Battery block 9V

nets:
  VIN: M1.VIN, Part1.5V, A1.+, DRV_2.VOLTAGE_DD
  GND: M1.GND, Part1.GND, S1.leg0, M2.GND, A1.-, DRV_2.GROUND_ST/_MT, DRV_2.GROUND_LOG, VCC2.-
  N1: M1.SCL, Part1.A5/SCL, M2.SCL
  N2: M1.SDA, Part1.A4/SDA, M2.SDA
  N3: Part1.D8, A1.Out
  N4: Part1.D9_PWM, S1.leg1
  N5: Part1.D2, M2.VIN
  N6: M3.A, DRV_2.OUT_1B
  N7: M3.C, DRV_2.OUT_1A
  N8: M3.B, DRV_2.OUT_2A
  N9: M3.D, DRV_2.OUT_2B
  N10: DRV_2.RESET, DRV_2.SLEEP
  N11: DRV_2.VOLTAGE_ST/_MT, VCC2.+

custom parts:
  BME280: Temperature Humidity Barometric presure Sensor
  MAX30102: Oximeter module using the MAX30102 chip. You may wish to read (and check your module) this post on power problems with these modules: https://reedpaper.wordpress.com/2018/08/22/pulse-oximeter-max30100-max30102-how-to-fix-wrong-board/ . As usual, if you want the mounting holes in pcb, you need to drag a hole over the pad in silkscreen to actually drill the hole (by default they are not drilled)
  DHT22 module: DHT22 module. Pins VCC Data GND.
